# Fritzing sketch Midi Drum Interface 2.0 (saved by Fritzing 0.9.3b)
perfboards: 1

parts:
  D1 = Rectifier Diode [part_number=1N4001 package="Melf DO-213 AB [SMD]"]
  D2 = Rectifier Diode [part_number=1N4001 package="Melf DO-213 AB [SMD]"]
  D3 = Rectifier Diode [part_number=1N4001 package="Melf DO-213 AB [SMD]"]
  D4 = Rectifier Diode [part_number=1N4001 package="Melf DO-213 AB [SMD]"]
  C1 = Capacitor Polarized [package=cpol-radial-10uf-25v]
  1/4"_audio_jack1 = AMPHENOL - ACJS-MHDR [package=ACJS-MHDR]

nets:
  N1: D1.cathode, D2.cathode, C1.+
  N2: D1.anode, D3.cathode, 1/4"_audio_jack1.Tip_(6)
  N3: D2.anode, D4.cathode, 1/4"_audio_jack1.Sleeve_(1), 1/4"_audio_jack1.Ring_(2), 1/4"_audio_jack1.Ring_(5)
  N4: D3.anode, D4.anode, C1.-

custom parts:
  AMPHENOL - ACJS-MHDR: 1/4" audio jack
